// Logisim project 10 bit ALU.circ as structural Verilog: 1 circuit, main circuit main
module main (
  input  [9:0] in_1,
  input  [9:0] in_2,
  input  [1:0] in_3,
  output [9:0] out_4
);

  wire [9:0] adder_1_out, divider_1_out, multiplier_1_out, subtractor_1_out;

  Adder #(.width(10)) adder_1 (.a(in_1), .b(in_2), .out(adder_1_out));  // open: cin, cout
  Subtractor #(.width(10)) subtractor_1 (.a(in_1), .b(in_2), .out(subtractor_1_out));  // open: bin, bout
  Multiplier #(.width(10)) multiplier_1 (.a(in_1), .b(in_2), .out(multiplier_1_out));  // open: cin, cout
  Divider #(.width(10)) divider_1 (.a(in_1), .b(in_2), .out(divider_1_out));  // open: upper, rem
  Multiplexer #(.select(2), .width(10)) multiplexer_1 (
    .in0(adder_1_out), .in1(subtractor_1_out), .in2(multiplier_1_out), .in3(divider_1_out), .out(out_4),
    .sel(in_3));  // open: en

  // Other names for the same wires on the sheet: AluOp[1:0] = in_3
endmodule
