// Logisim project Control Unit.circ as structural Verilog: 1 circuit, main circuit main
module main (
  input  [2:0] Select,
  output out_2,
  output [1:0] out_3,
  output out_4,
  output out_5
);

  Multiplexer #(.select(3), .width(5)) multiplexer_1 (
    .in0(5'b10011), .in1(5'b10001), .in2(5'b00010), .in3(5'b00110), .in4(5'b01010), .in5(5'b01110),
    .out({out_2, out_3, out_4, out_5}), .sel(Select));  // open: in6, in7, en
endmodule
