// Logisim project Main.circ as structural Verilog: 1 circuit, main circuit main
module main (
  output [9:0] out_1,
  output [9:0] out_2
);

  wire AluSrc, clk, decoder_1_out0, decoder_1_out1, decoder_1_out2, decoder_1_out3, MemRW, MemToReg,
       not_1_out;
  wire [0:0] rom_1_data;
  wire [1:0] AluOp, RD, RS, RT;
  wire [2:0] rom_1_data_2;
  wire [9:0] adder_1_out, bit_extender_1_out, main_1_out_4, multiplexer_3_out, multiplexer_4_out,
       multiplexer_5_out, ram_1_data, register_1_q, register_2_q, register_3_q, register_4_q, register_5_q;

  Adder #(.width(10)) adder_1 (.a(register_1_q), .b(10'h1), .out(adder_1_out));  // open: cin, cout
  Register #(.width(10)) register_1 (.D(adder_1_out), .Q(register_1_q), .clk(clk));  // open: en, clr
  Button button_1 (.out(clk));
  Control_Unit_main Control_Unit (
    .out_2(AluSrc), .out_3(AluOp), .out_4(MemRW), .out_5(MemToReg), .Select(rom_1_data_2));
  ROM #(.addrWidth(10), .dataWidth(10)) rom_1 (
    .addr(register_1_q), .data({rom_1_data_2, RD, RS, RT, rom_1_data[0]}));  // open: sel
  Decoder #(.select(2)) decoder_1 (
    .out0(decoder_1_out0), .out1(decoder_1_out1), .out2(decoder_1_out2), .out3(decoder_1_out3), .sel(RD));  // open: en
  assign bit_extender_1_out = {{8{1'b0}}, RT};  // Bit_Extender bit_extender_1
  Register #(.width(10)) register_2 (
    .D(multiplexer_5_out), .en(decoder_1_out0), .Q(register_2_q), .clk(clk));  // open: clr
  Register #(.width(10)) register_3 (
    .D(multiplexer_5_out), .en(decoder_1_out1), .Q(register_3_q), .clk(clk));  // open: clr
  Register #(.width(10)) register_4 (
    .D(multiplexer_5_out), .en(decoder_1_out2), .Q(register_4_q), .clk(clk));  // open: clr
  Register #(.width(10)) register_5 (
    .D(multiplexer_5_out), .en(decoder_1_out3), .Q(register_5_q), .clk(clk));  // open: clr
  Multiplexer #(.select(2), .width(10)) multiplexer_1 (
    .in0(register_2_q), .in1(register_3_q), .in2(register_4_q), .in3(register_5_q), .out(out_2), .sel(RS));  // open: en
  Multiplexer #(.select(2), .width(10)) multiplexer_2 (
    .in0(register_2_q), .in1(register_3_q), .in2(register_4_q), .in3(register_5_q), .out(out_1), .sel(RT));  // open: en
  Multiplexer #(.select(2), .width(10)) multiplexer_3 (
    .in0(register_2_q), .in1(register_3_q), .in2(register_4_q), .in3(register_5_q), .out(multiplexer_3_out),
    .sel(RD));  // open: en
  _10_bit_ALU_main main_1 (.in_1(out_2), .in_2(multiplexer_4_out), .out_4(main_1_out_4), .in_3(AluOp));
  Multiplexer #(.width(10)) multiplexer_4 (
    .in0(out_1), .in1(bit_extender_1_out), .out(multiplexer_4_out), .sel(AluSrc));  // open: en
  Multiplexer #(.width(10)) multiplexer_5 (
    .in0(main_1_out_4), .in1(ram_1_data), .out(multiplexer_5_out), .en(MemToReg));  // open: sel
  RAM #(.addrWidth(10), .dataWidth(10)) ram_1 (
    .addr(main_1_out_4), .data(ram_1_data), .clk(clk), .ld(MemRW));  // open: sel, clr
  assign ram_1_data = not_1_out ? multiplexer_3_out : 10'bz;  // Controlled_Buffer controlled_buffer_1
  not not_1 (not_1_out, MemRW);

  // Notes on the sheet:
  //   contents of rom_1 (hex, n*v repeats v):
  //   8 30 40 26c 1c6 2e2 10c 98
endmodule
